# Fritzing sketch Diagrama_fritzing (saved by Fritzing 0.9.5d)

parts:
  L298N1 = L298N DC motor driver
  M1 = DC Motor
  M2 = DC Motor
  Part1 = Bluetooth HC-05 Macho  # not connected
  Part2 = Arduino Uno (Rev3) - ICSP  # not connected
  HC-SR04_Sensor_1 = HC-SR04 Ultrasonic Distance Sensor  # not connected

nets:
  N1: L298N1.OUT1, M2.pin_2
  N2: L298N1.OUT2, M2.pin_1
  N3: L298N1.OUT3, M1.pin_2
  N4: L298N1.OUT4, M1.pin_1

notes:
  voltaje bateria
  Tierra
  duino - Vin
  duino - 4 digital
  duino - 6 digital
  duino - 5 digital
  duino - 7 digital
  duino - +5v
  duino - gnd
  duino - 11 digital
  duino - 10 digital
  gnd bateria
  L298N - 5v
  hc-05 - Rx
  hc-05 - Tx
  L298N - in 1
  L298N - in 2
  L298N - in 3
  L298N - in 4
  5v
  duino - 3 digital
  duino - 2 digital
  tierra
  ultrasonico - echo
  ultrasonico - trigger

custom parts:
  L298N DC motor driver: 2x DC motor driver with 78M05 positive voltage regulator (7..35 V) L298N: max 46 V, 2 A Set 5 V Enable jumper to enable 5 V regultor (needed for the L298N) and +5 V output at screw terminal or supply external +5 V at screw terminal Set ENA and/or ENB to +5 V to enable motor permanently or supply ENA and/or ENB with PWM signal IN1 and IN2 set rotation directory for motor A (OUT1/OUT2) IN2 and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
